# Fritzing sketch MIDTERM-PROJECT (saved by Fritzing 0.9.3b)
breadboards: 1

parts:
  R1 = Resistor [tolerance=±5% resistance=220 package=THT]
  R2 = Resistor [tolerance=±5% resistance=220 package=THT]
  R3 = Resistor [tolerance=±5% resistance=220 package=THT]
  R4 = Resistor [tolerance=±5% resistance=150 package=THT]
  R5 = Resistor [tolerance=±5% resistance=180 package=THT]
  R6 = Resistor [tolerance=±5% resistance=245 package=THT]
  Part1 = Arduino Mega 2560 (Rev3)

nets:
  N1: R1.Pin_0, R4.Pin_1, Part1.A2
  N2: R1.Pin_1, R2.Pin_1, R3.Pin_1, Part1.5V
  N3: R2.Pin_0, R5.Pin_1, Part1.A1
  N4: R3.Pin_0, R6.Pin_1, Part1.A0
  N5: R4.Pin_0, R5.Pin_0, R6.Pin_0, Part1.GND
